// Logisim project lab6.circ as structural Verilog: 6 circuits, main circuit main
module main (
  input  X1,
  input  X2,
  output y
);

  wire not_1_out, not_2_out, \И_2_out , \И_out ;

  not not_1 (not_1_out, X1);
  not not_2 (not_2_out, X2);
  and \u_И  (\И_out , not_1_out, X2);
  and \u_И_2  (\И_2_out , X1, not_2_out);
  or \u_ИЛИ  (y, \И_out , \И_2_out );

  // Notes on the sheet:
  //   НЕ
  //   НЕ
endmodule

module \полусумматор  (
  input  \Х1 ,
  input  \Х2 ,
  output out_3,
  output \Младший_разряд 
);

  and and_1 (out_3, \Х1 , \Х2 );
  main main_1 (.X1(\Х1 ), .X2(\Х2 ), .y(\Младший_разряд ));

  // Notes on the sheet:
  //   Схема сравнения
  //   Старший разряд перенос
endmodule

module \сумматор  (
  input  \Х1 ,
  input  \Х2 ,
  input  \Рi ,
  output P,
  output S
);

  wire \полусумматор_1_out_3 , \полусумматор_1_младший_разряд , \полусумматор_2_out_3 ;

  \полусумматор  \u_полусумматор_1  (
    .\Х1 (\Х1 ), .\Х2 (\Х2 ), .out_3(\полусумматор_1_out_3 ),
    .\Младший_разряд (\полусумматор_1_младший_разряд ));
  \полусумматор  \u_полусумматор_2  (
    .\Х1 (\полусумматор_1_младший_разряд ), .\Х2 (\Рi ), .out_3(\полусумматор_2_out_3 ), .\Младший_разряд (S));
  or \u_ИЛИ  (P, \полусумматор_1_out_3 , \полусумматор_2_out_3 );

  // Notes on the sheet:
  //   Полусумматор
  //   Полусумматор
endmodule

module \_4_сумматора  (
  input  in_1,
  input  in_2,
  input  in_3,
  input  in_4,
  input  in_5,
  input  in_6,
  input  in_7,
  input  in_8,
  input  in_9,
  output out_10,
  output out_11,
  output out_12,
  output out_13,
  output out_14
);

  wire \сумматор_2_p , \сумматор_4_p ;

  \сумматор  \u_сумматор_1  (.\Х1 (in_7), .\Х2 (in_8), .\Рi (in_9), .P(in_6), .S(out_14));
  \сумматор  \u_сумматор_2  (.\Х1 (in_5), .\Х2 (in_6), .\Рi (in_6), .P(\сумматор_2_p ), .S(out_13));
  \сумматор  \u_сумматор_3  (.\Х1 (in_1), .\Х2 (in_1), .\Рi (\сумматор_4_p ), .P(out_10), .S(out_11));
  \сумматор  \u_сумматор_4  (.\Х1 (in_3), .\Х2 (in_4), .\Рi (\сумматор_2_p ), .P(\сумматор_4_p ), .S(out_12));

  assign in_2 = in_1;
endmodule

module \рис_1  (
  input  in_1,
  input  in_2,
  output out_3,
  output out_4
);

  wire not_1_out, or_1_out;

  or or_1 (or_1_out, in_1, in_2);
  and and_1 (out_4, in_1, in_2);
  not not_1 (not_1_out, out_4);
  and and_2 (out_3, or_1_out, not_1_out);
endmodule

module \рис_2  (
  input  in_1,
  input  in_2,
  input  in_3,
  output out_4,
  output out_5
);

  wire and_1_out, and_2_out, and_3_out, and_4_out, and_5_out, not_1_out, or_1_out;

  and and_1 (and_1_out, in_1, in_2);
  and and_2 (and_2_out, in_1, in_3);
  and and_3 (and_3_out, in_2, in_3);
  or or_1 (or_1_out, in_1, in_2, in_3);
  and and_4 (and_4_out, in_1, in_2, in_3);
  or or_2 (out_4, and_1_out, and_2_out, and_3_out);
  not not_1 (not_1_out, out_4);
  and and_5 (and_5_out, not_1_out, or_1_out);
  or or_3 (out_5, and_5_out, and_4_out);
endmodule
